# Fritzing sketch Limbot (saved by Fritzing 0.9.2b)
breadboards: 1

parts:
  Part1 = Arduino Uno (Rev3) - ICSP
  Part2 = Bluetooth Module Breakout - Roving Networks (RN-41)
  1k = Resistor [tolerance=±5% resistance=220 package=THT]
  1k_2 = Resistor [tolerance=±5% resistance=220 package=THT]
  1k_3 = Resistor [tolerance=±5% resistance=220 package=THT]
  IC1 = H-Bridge [package=THT]
  მარჯვენა = DC Motor
  მარცხენა = DC Motor
  12ვ = LIPO-110mAh [package=lipo-110]

nets:
  5V: Part1.5V, Part2.VCC, IC1.VCC1
  N1: Part1.D9_PWM, IC1.1A
  N2: Part1.D10_PWM/SS, IC1.4A
  N3: Part1.D11_PWM/MOSI, IC1.3A
  GND: Part1.GND, Part2.GND, 1k_2.Pin_1, IC1.GND1, IC1.GND2, 12ვ.-
  N4: Part1.D0/RX, Part2.UARTTX
  N5: Part1.D1/TX, 1k_3.Pin_0
  N6: Part1.D3_PWM, IC1.2A
  N7: Part2.UARTRX, 1k.Pin_0, 1k_3.Pin_1
  N8: 1k.Pin_1, 1k_2.Pin_0
  N9: IC1.1Y, მარჯვენა.pin_1
  N10: IC1.2Y, მარჯვენა.pin_2
  N11: IC1.VCC2, 12ვ.+
  N12: IC1.3Y, მარცხენა.pin_2
  GND3: IC1.GND3, IC1.GND4
  N13: IC1.4Y, მარცხენა.pin_1
